// Logisim project 1.circ as structural Verilog: 1 circuit, main circuit main
module main (
);

  wire button_1_out, button_2_out, transistor_1_out, transistor_3_out, transistor_4_out;

  Button button_1 (.out(button_1_out));
  Button button_2 (.out(button_2_out));
  Transistor #(.\type ("n")) transistor_1 (.in(1'b1), .out(transistor_1_out), .gate(button_1_out));
  Transistor #(.\type ("n")) transistor_2 (.in(1'b1), .out(transistor_1_out), .gate(button_2_out));
  LED led_1 (.in(transistor_1_out));
  Transistor transistor_3 (.in(transistor_1_out), .out(transistor_3_out), .gate(button_1_out));
  Transistor transistor_4 (.in(transistor_3_out), .out(transistor_4_out), .gate(button_2_out));
  // also tied to GND on the sheet: transistor_4_out
endmodule
