// Logisim project CPU.circ as structural Verilog: 5 circuits, main circuit main
module main (
);

  wire and_1_out, and_2_out, button_1_out, button_2_out, cmp_1_output, decoder_1_out0, decoder_1_out1,
       program_logic_1_compare, program_logic_1_reg1_read_en, program_logic_1_reg2_read_en,
       program_logic_1_reg_bank_sel, program_logic_1_reg_write_en;
  wire [1:0] program_logic_1_reg1_sel, program_logic_1_reg2_sel;
  wire [3:0] multiplexer_1_out, multiplexer_2_out, program_logic_1_output1, register_bank_1_reg1_output,
       register_bank_1_reg2_output, register_bank_2_reg1_output, register_bank_2_reg2_output;

  Program_Logic program_logic_1 (
    .clock(button_1_out), .reset(button_2_out), .Output1(program_logic_1_output1),
    .Reg2_Sel(program_logic_1_reg2_sel), .Reg1_Sel(program_logic_1_reg1_sel),
    .Reg2_Read_En(program_logic_1_reg2_read_en), .Reg1_Read_En(program_logic_1_reg1_read_en),
    .Reg_Write_En(program_logic_1_reg_write_en), .Compare(program_logic_1_compare),
    .Jmp_Fnct_Sel(cmp_1_output), .Jmp_En(cmp_1_output), .Reg_Input_1(multiplexer_1_out),
    .Reg_Input_2(multiplexer_2_out), .Reg_Bank_Sel(program_logic_1_reg_bank_sel));  // open: Output2
  Button button_1 (.out(button_1_out));
  Button button_2 (.out(button_2_out));
  Decoder #(.enable("false")) decoder_1 (
    .out0(decoder_1_out0), .out1(decoder_1_out1), .sel(program_logic_1_reg_bank_sel));
  Register_Bank register_bank_1 (
    .reset(button_2_out), .Write_Select(program_logic_1_reg1_sel), .Write_Enable(and_1_out),
    .Input(program_logic_1_output1), .Reg1_Output(register_bank_1_reg1_output),
    .Read_Reg1_En(program_logic_1_reg1_read_en), .Read_Reg1_Sel(program_logic_1_reg1_sel),
    .Reg2_Output(register_bank_1_reg2_output), .Read_Reg2_En(program_logic_1_reg2_read_en),
    .Read_Reg2_Sel(program_logic_1_reg2_sel));  // open: Reg_11, Reg_10, Reg_01, Reg_00
  and and_1 (and_1_out, program_logic_1_reg_write_en, decoder_1_out0);
  Register_Bank register_bank_2 (
    .reset(button_2_out), .Write_Select(program_logic_1_reg1_sel), .Write_Enable(and_2_out),
    .Input(program_logic_1_output1), .Reg1_Output(register_bank_2_reg1_output),
    .Read_Reg1_En(program_logic_1_reg1_read_en), .Read_Reg1_Sel(program_logic_1_reg1_sel),
    .Reg2_Output(register_bank_2_reg2_output), .Read_Reg2_En(program_logic_1_reg2_read_en),
    .Read_Reg2_Sel(program_logic_1_reg2_sel));  // open: Reg_11, Reg_10, Reg_01, Reg_00
  and and_2 (and_2_out, program_logic_1_reg_write_en, decoder_1_out1);
  cmp cmp_1 (
    .En(program_logic_1_compare), .Input_1(multiplexer_1_out), .Input_2(multiplexer_2_out),
    .Output(cmp_1_output));
  Multiplexer #(.width(4), .enable("false")) multiplexer_1 (
    .in0(register_bank_1_reg1_output), .in1(register_bank_2_reg1_output), .out(multiplexer_1_out),
    .sel(program_logic_1_reg_bank_sel));
  Multiplexer #(.width(4), .enable("false")) multiplexer_2 (
    .in0(register_bank_1_reg2_output), .in1(register_bank_2_reg2_output), .out(multiplexer_2_out),
    .sel(program_logic_1_reg_bank_sel));
  // Probe on register_bank_1_reg1_output
  // Probe on register_bank_1_reg2_output
  // Probe on register_bank_2_reg1_output
  // Probe on register_bank_2_reg2_output

  // Notes on the sheet:
  //   Program Logic
  //   Register Bank
endmodule

module Program_Logic (
  input  [3:0] Reg_Input_1,
  input  [3:0] Reg_Input_2,
  input  clock,
  input  reset,
  input  Jmp_En,
  input  Jmp_Fnct_Sel,
  output [3:0] Output2,
  output [3:0] Output1,
  output [1:0] Reg2_Sel,
  output [1:0] Reg1_Sel,
  output Reg_Bank_Sel,
  output Reg2_Read_En,
  output Reg1_Read_En,
  output Reg_Write_En,
  output Compare
);

  wire or_1_out;
  wire [0:0] or_2_out;
  wire [7:0] arithmics_1_output, multiplexer_1_out, register_1_q;
  wire [20:0] rom_1_data;

  Multiplexer #(.width(8), .enable("false")) multiplexer_1 (
    .in0(8'h1), .in1({4'b0000, Output1}), .out(multiplexer_1_out), .sel(or_1_out));
  Arithmics arithmics_1 (
    .Input_1(register_1_q), .Input_2(multiplexer_1_out), .Function_Select({1'b0, or_2_out[0]}),
    .Output(arithmics_1_output));  // open: Enable
  // Probe on arithmics_1_output
  or or_1 (or_1_out, rom_1_data[20], Jmp_En);
  or or_2 (or_2_out[0], rom_1_data[19], Jmp_Fnct_Sel);
  Register register_1 (.D(arithmics_1_output), .Q(register_1_q), .clk(clock), .clr(reset));  // open: en
  Multiplexer #(.width(4), .disabled(0), .enable("false")) multiplexer_2 (
    .in0(rom_1_data[7:4]), .in1(Reg_Input_1), .out(Output1), .sel(rom_1_data[13]));
  ROM #(.dataWidth(21)) rom_1 (
    .addr(register_1_q),
    .data({rom_1_data[20:19], Compare, Reg_Write_En, Reg1_Read_En, Reg2_Read_En, Reg_Bank_Sel, rom_1_data[13:12], Reg1_Sel, Reg2_Sel, rom_1_data[7:0]}));  // open: sel
  Multiplexer #(.width(4), .disabled(0), .enable("false")) multiplexer_3 (
    .in0(rom_1_data[3:0]), .in1(Reg_Input_2), .out(Output2), .sel(rom_1_data[12]));

  // Notes on the sheet:
  //   contents of rom_1 (hex, n*v repeats v):
  //   18800 38860 3c860
endmodule

module Register_Bank (
  input  [1:0] Write_Select,
  input  Write_Enable,
  input  Read_Reg1_En,
  input  [1:0] Read_Reg1_Sel,
  input  Read_Reg2_En,
  input  [3:0] Input,
  input  reset,
  input  [1:0] Read_Reg2_Sel,
  output [3:0] Reg1_Output,
  output [3:0] Reg_11,
  output [3:0] Reg_10,
  output [3:0] Reg_01,
  output [3:0] Reg_00,
  output [3:0] Reg2_Output
);

  wire decoder_1_out0, decoder_1_out1, decoder_1_out2, decoder_1_out3, not_1_out, not_2_out, not_3_out,
       not_4_out;

  Decoder #(.select(2), .disabled(0)) decoder_1 (
    .out0(decoder_1_out0), .out1(decoder_1_out1), .out2(decoder_1_out2), .out3(decoder_1_out3),
    .sel(Write_Select), .en(Write_Enable));
  not not_1 (not_1_out, decoder_1_out3);
  Register #(.width(4), .trigger("high")) register_1 (
    .D(Input), .en(not_1_out), .Q(Reg_11), .clk(decoder_1_out3), .clr(reset));
  Register #(.width(4), .trigger("high")) register_2 (
    .D(Input), .en(not_2_out), .Q(Reg_10), .clk(decoder_1_out2), .clr(reset));
  not not_2 (not_2_out, decoder_1_out2);
  not not_3 (not_3_out, decoder_1_out1);
  Register #(.width(4), .trigger("high")) register_3 (
    .D(Input), .en(not_3_out), .Q(Reg_01), .clk(decoder_1_out1), .clr(reset));
  Register #(.width(4), .trigger("high")) register_4 (
    .D(Input), .en(not_4_out), .Q(Reg_00), .clk(decoder_1_out0), .clr(reset));
  not not_4 (not_4_out, decoder_1_out0);
  Multiplexer #(.select(2), .width(4)) multiplexer_1 (
    .in0(Reg_00), .in1(Reg_01), .in2(Reg_10), .in3(Reg_11), .out(Reg1_Output), .sel(Read_Reg1_Sel),
    .en(Read_Reg1_En));
  Multiplexer #(.select(2), .width(4)) multiplexer_2 (
    .in0(Reg_00), .in1(Reg_01), .in2(Reg_10), .in3(Reg_11), .out(Reg2_Output), .sel(Read_Reg2_Sel),
    .en(Read_Reg2_En));
endmodule

module Arithmics (
  input  [7:0] Input_1,
  input  [7:0] Input_2,
  input  Enable,
  input  [1:0] Function_Select,
  output [7:0] Output
);

  wire [7:0] adder_1_out, divider_1_out, multiplier_1_out, subtractor_1_out;

  Adder adder_1 (.a(Input_1), .b(Input_2), .out(adder_1_out));  // open: cin, cout
  Subtractor subtractor_1 (.a(Input_1), .b(Input_2), .out(subtractor_1_out));  // open: bin, bout
  Multiplier multiplier_1 (.a(Input_1), .b(Input_2), .out(multiplier_1_out));  // open: cin, cout
  Divider divider_1 (.a(Input_1), .b(Input_2), .out(divider_1_out));  // open: upper, rem
  Multiplexer #(.select(2), .width(8)) multiplexer_1 (
    .in0(adder_1_out), .in1(subtractor_1_out), .in2(multiplier_1_out), .in3(divider_1_out), .out(Output),
    .sel(Function_Select), .en(Enable));
endmodule

module cmp (
  input  En,
  input  [3:0] Input_1,
  input  [3:0] Input_2,
  output Output
);

  wire comparator_1_eq, comparator_1_gt, or_1_out;

  Comparator #(.width(4)) comparator_1 (
    .a(Input_1), .b(Input_2), .gt(comparator_1_gt), .eq(comparator_1_eq));  // open: lt
  Multiplexer #(.disabled(0), .enable("false")) multiplexer_1 (.in0(1'b0), .in1(or_1_out), .out(Output), .sel(En));
  or or_1 (or_1_out, comparator_1_gt, comparator_1_eq);
endmodule
